# Fritzing sketch wemos_dual_watchdog (saved by Fritzing 0.9.3b)
circuit board: 10cm x 6cm
breadboards: 1

parts:
  J1 = female pin header, 8 pins [form="♀ (female)"]  # not connected
  J2 = female pin header, 8 pins [form="♀ (female)"]
  J3 = screw terminal, 2 pins
  HLK-PM1 = HLK-PM01
  R1 = Resistor [tolerance=±5% resistance=220 package=THT]
  LED1 = LED - 5mm [color="Red (633nm)" package="5 mm [THT]"]
  J9 = female pin header, 8 pins [form="♀ (female)"]
  J10 = female pin header, 8 pins [form="♀ (female)"]
  J11 = female pin header, 8 pins [form="♀ (female)"]
  J12 = female pin header, 8 pins [form="♀ (female)"]  # not connected
  J13 = female pin header, 4 pins [form="♀ (female)"]
  J14 = female pin header, 4 pins [form="♀ (female)"]

nets:
  N1: J2.pin3, J10.pin3
  N2: J2.pin7, HLK-PM1.-Vo, LED1.cathode, J10.pin7, J11.pin7, J13.pin4, J14.pin1
  N3: J2.pin8, HLK-PM1.+Vo, R1.Pin_0, J10.pin8, J11.pin8
  N4: J3.pin1, HLK-PM1.AC#1
  N5: J3.pin2, HLK-PM1.AC#0
  N6: R1.Pin_1, LED1.anode
  N7: J9.pin1, J13.pin1
  N8: J9.pin3, J14.pin4
  N9: J9.pin4, J14.pin3
  N10: J9.pin5, J14.pin2
  N11: J9.pin7, J13.pin2
  N12: J9.pin8, J13.pin3
  N13: J10.pin4, J11.pin3

notes:
  5V
  tihc
  240VAC
  Rly 2
  Rly 1
